# Fritzing sketch schematic (saved by Fritzing 1.0.0rc)
circuit board: 8.46667cm x 5.64444cm
breadboards: 1

parts:
  R1 = Trimmer Potentiometer [maximum_resistance=10kΩ knob_status=50% power=0.5W package=THT]
  Mod1 = ESP32-TTGO-T-DISPLAY

nets:
  N1: R1.leg1, Mod1.G-1, Mod1.G-2, Mod1.G-10, Mod1.G-11, Mod1.G-14
  N2: R1.wiper, Mod1.36
  N3: R1.leg2, Mod1.3V

custom parts:
  ESP32-TTGO-T-DISPLAY: LILYGO TTGO T-Display GD32VF103CBT6 Main Chip ST7789 1.14 Inch IPS 240x135 Resolution Minimalist Development Board.
